# Fritzing sketch CircuitSketch (saved by Fritzing 0.9.5d)

parts:
  Parça1 = Arduino Uno (Rev3)
  U1 = LCD-16X2 [package=lcd-16x2]
  LCM1602_IIC1 = LCM1602 IIC [part_number="LCM1602 IIC" chip_label="LCM1602 IIC" package="DIP (Dual Inline) [THT]"]
  HC-SR04_Sensor_1 = HC-SR04 Ultrasonic Distance Sensor
  J1 = Piezo Speaker

nets:
  N1: Parça1.A4/SDA, LCM1602_IIC1.SDA
  N2: Parça1.A5/SCL, LCM1602_IIC1.SCL
  N3: Parça1.D11_PWM/MOSI, HC-SR04_Sensor_1.ECHO
  N4: Parça1.D12/MISO, HC-SR04_Sensor_1.TRIG
  GND: Parça1.GND, LCM1602_IIC1.GND, HC-SR04_Sensor_1.GND, J1.pin1
  N5: Parça1.D2, J1.pin2
  VCC: Parça1.5V, LCM1602_IIC1.VCC, HC-SR04_Sensor_1.VCC
  VSS: U1.VSS, LCM1602_IIC1.VSS
  VDD: U1.VDD, LCM1602_IIC1.VDD
  N6: U1.VO, LCM1602_IIC1.V0
  N7: U1.RS, LCM1602_IIC1.RS
  N8: U1.R_W, LCM1602_IIC1.RW
  N9: U1.E, LCM1602_IIC1.E
  N10: U1.DB0, LCM1602_IIC1.D0
  N11: U1.DB1, LCM1602_IIC1.D1
  N12: U1.DB2, LCM1602_IIC1.D2
  N13: U1.DB3, LCM1602_IIC1.D3
  N14: U1.DB4, LCM1602_IIC1.D4
  N15: U1.DB5, LCM1602_IIC1.D5
  N16: U1.DB6, LCM1602_IIC1.D6
  N17: U1.DB7, LCM1602_IIC1.D7
  N18: U1.A, LCM1602_IIC1.A
  N19: U1.K, LCM1602_IIC1.K

custom parts:
  LCM1602 IIC: I2C-Module to use a 1602 or 2004 LCD on with the wire.h libory Serial LCD Modul
